# Fritzing sketch part1sketch (saved by Fritzing 0.9.9b)
breadboards: 1

parts:
  Part1 = Arduino Uno (Rev3) - ICSP
  LED1 = LED - 5mm [color="Red (633nm)" current=0.030 package="5 mm [THT]"]
  R1 = Resistor [tolerance=±5% power=0.25 resistance=1.6k package=THT]

nets:
  N1: Part1.D12/MISO, R1.Pin_0
  N2: Part1.GND, LED1.anode
  N3: LED1.cathode, R1.Pin_1
