# Fritzing sketch part2sketch (saved by Fritzing 0.9.9b)
breadboards: 1

parts:
  Part1 = Arduino Uno (Rev3) - ICSP
  LED1 = LED - 5mm [color="Red (633nm)" current=0.030 package="5 mm [THT]"]
  R1 = Resistor [tolerance=±5% power=0.25 resistance=1.6k package=THT]
  LED2 = LED - 5mm [color="Blue (470nm)" current=0.030 package="5 mm [THT]"]
  R2 = Resistor [tolerance=±5% power=0.25 resistance=1.6k package=THT]
  R3 = Resistor [tolerance=±5% power=0.25 resistance=1.6k package=THT]
  LED3 = LED - 5mm [color="Green (560nm)" current=0.030 package="5 mm [THT]"]

nets:
  N1: Part1.D8, R2.Pin_0
  N2: Part1.D12/MISO, R1.Pin_0
  N3: Part1.GND, LED1.anode
  N4: Part1.D4, R3.Pin_0
  N5: LED1.cathode, R1.Pin_1
  N6: LED2.cathode, R2.Pin_1
  N7: LED2.anode, LED3.anode
  N8: R3.Pin_1, LED3.cathode
