# Fritzing sketch pulldownsketch (saved by Fritzing 0.9.9b)
breadboards: 1

parts:
  Part1 = Arduino Uno (Rev3) - ICSP
  S1 = Pushbutton [package="[THT]"]
  R1 = Resistor [tolerance=±5% power=0.25 resistance=10k package=THT]

nets:
  N1: Part1.D12/MISO, S1.Pin_1, S1.Pin_2, R1.Pin_0
  N2: Part1.GND, R1.Pin_1
  N3: Part1.5V, S1.Pin_3, S1.Pin_4
